// Logisim project Polla.circ as structural Verilog: 1 circuit, main circuit main
module main (
);

  wire and_1_out, and_2_out, and_3_out, and_4_out, and_5_out, and_6_out, and_7_out, and_8_out, and_9_out,
       and_10_out, and_11_out, and_12_out, and_13_out, and_14_out, and_15_out, and_16_out, and_17_out,
       and_18_out, and_19_out, and_20_out, and_21_out, and_22_out, and_23_out, and_24_out, and_25_out,
       and_26_out, and_27_out, and_28_out, and_29_out, and_30_out, dipswitch_1_sw1, dipswitch_1_sw2,
       dipswitch_1_sw3, dipswitch_1_sw4, dipswitch_1_sw5, dipswitch_1_sw6, dipswitch_1_sw7, dipswitch_1_sw8,
       dipswitch_2_sw1, dipswitch_2_sw2, dipswitch_2_sw3, dipswitch_2_sw4, dipswitch_2_sw5, dipswitch_2_sw6,
       dipswitch_2_sw7, dipswitch_2_sw8, or_1_out, or_2_out, or_3_out, or_4_out, or_5_out, or_6_out,
       or_7_out, or_8_out, or_9_out, or_10_out, or_11_out, or_12_out, or_13_out, or_14_out,
       pull_resistor_1_node, pull_resistor_2_node, pull_resistor_3_node, pull_resistor_4_node,
       pull_resistor_5_node, pull_resistor_6_node, pull_resistor_7_node, pull_resistor_8_node,
       pull_resistor_9_node, pull_resistor_10_node, pull_resistor_11_node, pull_resistor_12_node,
       pull_resistor_13_node, pull_resistor_14_node, pull_resistor_15_node, pull_resistor_16_node, xor_1_out,
       xor_2_out, xor_3_out, xor_4_out, xor_5_out, xor_6_out, xor_7_out, xor_8_out, xor_9_out, xor_10_out,
       xor_11_out, xor_12_out, xor_13_out, xor_14_out, xor_15_out, xor_16_out, xor_17_out, xor_18_out,
       xor_19_out, xor_20_out, xor_21_out, xor_22_out, xor_23_out, xor_24_out, xor_25_out, xor_26_out,
       xor_27_out, xor_28_out, xor_29_out, xor_30_out;

  LED led_1 (.in(xor_1_out));
  LED led_2 (.in(xor_3_out));
  LED led_3 (.in(xor_7_out));
  LED led_4 (.in(xor_10_out));
  LED led_5 (.in(xor_14_out));
  DipSwitch dipswitch_1 (
    .sw1(dipswitch_1_sw1), .sw2(dipswitch_1_sw2), .sw3(dipswitch_1_sw3), .sw4(dipswitch_1_sw4),
    .sw5(dipswitch_1_sw5), .sw6(dipswitch_1_sw6), .sw7(dipswitch_1_sw7), .sw8(dipswitch_1_sw8));
  LED led_6 (.in(xor_17_out));
  LED led_7 (.in(xor_21_out));
  LED led_8 (.in(xor_24_out));
  LED led_9 (.in(or_11_out));
  DipSwitch dipswitch_2 (
    .sw1(dipswitch_2_sw1), .sw2(dipswitch_2_sw2), .sw3(dipswitch_2_sw3), .sw4(dipswitch_2_sw4),
    .sw5(dipswitch_2_sw5), .sw6(dipswitch_2_sw6), .sw7(dipswitch_2_sw7), .sw8(dipswitch_2_sw8));
  Pull_Resistor pull_resistor_1 (.node(pull_resistor_1_node));
  // Switch A11: pin names not known; wires that end beside it: 1'b1, pull_resistor_1_node
  Pull_Resistor pull_resistor_2 (.node(pull_resistor_2_node));
  // Switch B11: pin names not known; wires that end beside it: 1'b1, pull_resistor_2_node
  Pull_Resistor pull_resistor_3 (.node(pull_resistor_3_node));
  // Switch A22: pin names not known; wires that end beside it: 1'b1, pull_resistor_3_node
  Pull_Resistor pull_resistor_4 (.node(pull_resistor_4_node));
  // Switch B22: pin names not known; wires that end beside it: 1'b1, pull_resistor_4_node
  Pull_Resistor pull_resistor_5 (.node(pull_resistor_5_node));
  // Switch A33: pin names not known; wires that end beside it: 1'b1, pull_resistor_5_node
  Pull_Resistor pull_resistor_6 (.node(pull_resistor_6_node));
  // Switch B33: pin names not known; wires that end beside it: 1'b1, pull_resistor_6_node
  Pull_Resistor pull_resistor_7 (.node(pull_resistor_7_node));
  // Switch A44: pin names not known; wires that end beside it: 1'b1, pull_resistor_7_node
  Pull_Resistor pull_resistor_8 (.node(pull_resistor_8_node));
  // Switch B44: pin names not known; wires that end beside it: 1'b1, pull_resistor_8_node
  Pull_Resistor pull_resistor_9 (.node(pull_resistor_9_node));
  // Switch A55: pin names not known; wires that end beside it: 1'b1, pull_resistor_9_node
  Pull_Resistor pull_resistor_10 (.node(pull_resistor_10_node));
  // Switch B55: pin names not known; wires that end beside it: 1'b1, pull_resistor_10_node
  Pull_Resistor pull_resistor_11 (.node(pull_resistor_11_node));
  // Switch A66: pin names not known; wires that end beside it: 1'b1, pull_resistor_11_node
  Pull_Resistor pull_resistor_12 (.node(pull_resistor_12_node));
  // Switch B66: pin names not known; wires that end beside it: 1'b1, pull_resistor_12_node
  Pull_Resistor pull_resistor_13 (.node(pull_resistor_13_node));
  // Switch A77: pin names not known; wires that end beside it: 1'b1, pull_resistor_13_node
  Pull_Resistor pull_resistor_14 (.node(pull_resistor_14_node));
  // Switch B77: pin names not known; wires that end beside it: 1'b1, pull_resistor_14_node
  Pull_Resistor pull_resistor_15 (.node(pull_resistor_15_node));
  // Switch A88: pin names not known; wires that end beside it: 1'b1, pull_resistor_15_node
  Pull_Resistor pull_resistor_16 (.node(pull_resistor_16_node));
  // Switch B88: pin names not known; wires that end beside it: 1'b1, pull_resistor_16_node
  Pull_Resistor pull_resistor_17 (.node(dipswitch_1_sw8));
  Pull_Resistor pull_resistor_18 (.node(dipswitch_2_sw8));
  Pull_Resistor pull_resistor_19 (.node(dipswitch_1_sw7));
  Pull_Resistor pull_resistor_20 (.node(dipswitch_2_sw7));
  Pull_Resistor pull_resistor_21 (.node(dipswitch_1_sw6));
  Pull_Resistor pull_resistor_22 (.node(dipswitch_2_sw6));
  Pull_Resistor pull_resistor_23 (.node(dipswitch_1_sw5));
  Pull_Resistor pull_resistor_24 (.node(dipswitch_2_sw5));
  Pull_Resistor pull_resistor_25 (.node(dipswitch_1_sw4));
  Pull_Resistor pull_resistor_26 (.node(dipswitch_2_sw4));
  Pull_Resistor pull_resistor_27 (.node(dipswitch_1_sw3));
  Pull_Resistor pull_resistor_28 (.node(dipswitch_2_sw3));
  Pull_Resistor pull_resistor_29 (.node(dipswitch_1_sw2));
  Pull_Resistor pull_resistor_30 (.node(dipswitch_2_sw2));
  Pull_Resistor pull_resistor_31 (.node(dipswitch_1_sw1));
  Pull_Resistor pull_resistor_32 (.node(dipswitch_2_sw1));
  xor xor_1 (xor_1_out, dipswitch_1_sw8, dipswitch_2_sw8);
  and and_1 (and_1_out, dipswitch_2_sw8, ~dipswitch_1_sw8);  // AND_Gate
  xor xor_2 (xor_2_out, and_1_out, dipswitch_1_sw7);
  and and_2 (and_2_out, and_1_out, ~dipswitch_1_sw7);  // AND_Gate
  and and_3 (and_3_out, pull_resistor_1_node, pull_resistor_2_node);
  xor xor_3 (xor_3_out, xor_2_out, dipswitch_2_sw7);
  and and_4 (and_4_out, dipswitch_2_sw7, ~xor_2_out);  // AND_Gate
  xor xor_4 (xor_4_out, pull_resistor_1_node, pull_resistor_2_node);
  or or_1 (or_1_out, and_4_out, and_2_out);
  and and_5 (and_5_out, ~or_1_out, dipswitch_1_sw6);  // AND_Gate
  xor xor_5 (xor_5_out, and_3_out, pull_resistor_3_node);
  and and_6 (and_6_out, and_3_out, pull_resistor_3_node);
  xor xor_6 (xor_6_out, or_1_out, dipswitch_1_sw6);
  xor xor_7 (xor_7_out, xor_6_out, dipswitch_2_sw6);
  and and_7 (and_7_out, dipswitch_2_sw6, ~xor_6_out);  // AND_Gate
  or or_2 (or_2_out, and_7_out, and_5_out);
  xor xor_8 (xor_8_out, xor_5_out, pull_resistor_4_node);
  and and_8 (and_8_out, pull_resistor_4_node, xor_5_out);
  xor xor_9 (xor_9_out, or_2_out, dipswitch_1_sw5);
  and and_9 (and_9_out, ~or_2_out, dipswitch_1_sw5);  // AND_Gate
  or or_3 (or_3_out, and_8_out, and_6_out);
  xor xor_10 (xor_10_out, xor_9_out, dipswitch_2_sw5);
  and and_10 (and_10_out, dipswitch_2_sw5, ~xor_9_out);  // AND_Gate
  xor xor_11 (xor_11_out, or_3_out, pull_resistor_5_node);
  and and_11 (and_11_out, or_3_out, pull_resistor_5_node);
  or or_4 (or_4_out, and_10_out, and_9_out);
  xor xor_12 (xor_12_out, or_4_out, dipswitch_1_sw4);
  and and_12 (and_12_out, ~or_4_out, dipswitch_1_sw4);  // AND_Gate
  xor xor_13 (xor_13_out, xor_11_out, pull_resistor_6_node);
  and and_13 (and_13_out, pull_resistor_6_node, xor_11_out);
  xor xor_14 (xor_14_out, xor_12_out, dipswitch_2_sw4);
  and and_14 (and_14_out, dipswitch_2_sw4, ~xor_12_out);  // AND_Gate
  or or_5 (or_5_out, and_13_out, and_11_out);
  or or_6 (or_6_out, and_14_out, and_12_out);
  xor xor_15 (xor_15_out, or_5_out, pull_resistor_7_node);
  and and_15 (and_15_out, or_5_out, pull_resistor_7_node);
  xor xor_16 (xor_16_out, or_6_out, dipswitch_1_sw3);
  and and_16 (and_16_out, ~or_6_out, dipswitch_1_sw3);  // AND_Gate
  xor xor_17 (xor_17_out, xor_16_out, dipswitch_2_sw3);
  and and_17 (and_17_out, dipswitch_2_sw3, ~xor_16_out);  // AND_Gate
  xor xor_18 (xor_18_out, xor_15_out, pull_resistor_8_node);
  and and_18 (and_18_out, pull_resistor_8_node, xor_15_out);
  or or_7 (or_7_out, and_17_out, and_16_out);
  and and_19 (and_19_out, ~or_7_out, dipswitch_1_sw2);  // AND_Gate
  or or_8 (or_8_out, and_18_out, and_15_out);
  xor xor_19 (xor_19_out, or_7_out, dipswitch_1_sw2);
  xor xor_20 (xor_20_out, or_8_out, pull_resistor_9_node);
  and and_20 (and_20_out, or_8_out, pull_resistor_9_node);
  xor xor_21 (xor_21_out, xor_19_out, dipswitch_2_sw2);
  and and_21 (and_21_out, dipswitch_2_sw2, ~xor_19_out);  // AND_Gate
  or or_9 (or_9_out, and_21_out, and_19_out);
  xor xor_22 (xor_22_out, or_9_out, dipswitch_1_sw1);
  and and_22 (and_22_out, ~or_9_out, dipswitch_1_sw1);  // AND_Gate
  xor xor_23 (xor_23_out, xor_20_out, pull_resistor_10_node);
  and and_23 (and_23_out, pull_resistor_10_node, xor_20_out);
  xor xor_24 (xor_24_out, xor_22_out, dipswitch_2_sw1);
  and and_24 (and_24_out, dipswitch_2_sw1, ~xor_22_out);  // AND_Gate
  or or_10 (or_10_out, and_23_out, and_20_out);
  or or_11 (or_11_out, and_24_out, and_22_out);
  xor xor_25 (xor_25_out, or_10_out, pull_resistor_11_node);
  and and_25 (and_25_out, or_10_out, pull_resistor_11_node);
  xor xor_26 (xor_26_out, xor_25_out, pull_resistor_12_node);
  and and_26 (and_26_out, pull_resistor_12_node, xor_25_out);
  or or_12 (or_12_out, and_26_out, and_25_out);
  xor xor_27 (xor_27_out, or_12_out, pull_resistor_13_node);
  and and_27 (and_27_out, or_12_out, pull_resistor_13_node);
  xor xor_28 (xor_28_out, xor_27_out, pull_resistor_14_node);
  and and_28 (and_28_out, pull_resistor_14_node, xor_27_out);
  or or_13 (or_13_out, and_28_out, and_27_out);
  xor xor_29 (xor_29_out, or_13_out, pull_resistor_15_node);
  and and_29 (and_29_out, or_13_out, pull_resistor_15_node);
  LED led_10 (.in(xor_4_out));
  LED led_11 (.in(xor_8_out));
  LED led_12 (.in(xor_13_out));
  LED led_13 (.in(xor_18_out));
  LED led_14 (.in(xor_23_out));
  LED led_15 (.in(xor_26_out));
  LED led_16 (.in(xor_28_out));
  LED led_17 (.in(xor_30_out));
  LED led_18 ();  // open: in
  LED led_19 ();  // open: in
  LED led_20 ();  // open: in
  LED led_21 ();  // open: in
  LED led_22 ();  // open: in
  LED led_23 ();  // open: in
  LED led_24 ();  // open: in
  LED led_25 ();  // open: in
  LED led_26 (.in(or_14_out));
  LED led_27 ();  // open: in
  xor xor_30 (xor_30_out, xor_29_out, pull_resistor_16_node);
  and and_30 (and_30_out, pull_resistor_16_node, xor_29_out);
  or or_14 (or_14_out, and_30_out, and_29_out);
endmodule
